// Logisim project 8_Bit_CAlculator.circ as structural Verilog: 8 circuits, main circuit main
module main (
  input  [7:0] in_1,
  input  [1:0] in_2,
  input  [7:0] in_3
);

  wire hex_display_1_out_5, hex_display_1_out_6, hex_display_1_out_7, hex_display_1_out_8,
       hex_display_1_out_9, hex_display_1_out_10, hex_display_1_out_11, hex_display_2_out_5,
       hex_display_2_out_6, hex_display_2_out_7, hex_display_2_out_8, hex_display_2_out_9,
       hex_display_2_out_10, hex_display_2_out_11, hex_display_3_out_5, hex_display_3_out_6,
       hex_display_3_out_7, hex_display_3_out_8, hex_display_3_out_9, hex_display_3_out_10,
       hex_display_3_out_11, hex_display_4_out_5, hex_display_4_out_6, hex_display_4_out_7,
       hex_display_4_out_8, hex_display_4_out_9, hex_display_4_out_10, hex_display_4_out_11;
  wire [8:0] n8_bit_adder_1_out_4, n8bit_subtractor_1_s0;
  wire [15:0] bit_divider_1_r0, multiplexer_1_out, n8bit_multiplier_1_s0;

  _8BIT_MULTIPLIER u_8bit_multiplier_1 (
    .in_1(in_3), .in_2(in_1), .S15(n8bit_multiplier_1_s0[15]), .S14(n8bit_multiplier_1_s0[14]),
    .S13(n8bit_multiplier_1_s0[13]), .S12(n8bit_multiplier_1_s0[12]), .S11(n8bit_multiplier_1_s0[11]),
    .S10(n8bit_multiplier_1_s0[10]), .S9(n8bit_multiplier_1_s0[9]), .S8(n8bit_multiplier_1_s0[8]),
    .S7(n8bit_multiplier_1_s0[7]), .S6(n8bit_multiplier_1_s0[6]), .S5(n8bit_multiplier_1_s0[5]),
    .S4(n8bit_multiplier_1_s0[4]), .S3(n8bit_multiplier_1_s0[3]), .S2(n8bit_multiplier_1_s0[2]),
    .S1(n8bit_multiplier_1_s0[1]), .S0(n8bit_multiplier_1_s0[0]));
  _8_bit_adder u_8_bit_adder_1 (
    .out_4(n8_bit_adder_1_out_4[0]), .in_2(in_1), .out_5(n8_bit_adder_1_out_4[1]),
    .out_6(n8_bit_adder_1_out_4[2]), .out_7(n8_bit_adder_1_out_4[3]), .out_8(n8_bit_adder_1_out_4[4]),
    .in_3(in_3), .out_9(n8_bit_adder_1_out_4[5]), .out_10(n8_bit_adder_1_out_4[6]),
    .out_11(n8_bit_adder_1_out_4[7]), .out_12(n8_bit_adder_1_out_4[8]), .in_1(1'b0));
  _8bit_subtractor u_8bit_subtractor_1 (
    .S0(n8bit_subtractor_1_s0[0]), .S1(n8bit_subtractor_1_s0[1]), .in_1(in_1), .S2(n8bit_subtractor_1_s0[2]),
    .S3(n8bit_subtractor_1_s0[3]), .S4(n8bit_subtractor_1_s0[4]), .S5(n8bit_subtractor_1_s0[5]),
    .S6(n8bit_subtractor_1_s0[6]), .S7(n8bit_subtractor_1_s0[7]),
    ._0_POSITIVE_1_NEGATIVE(n8bit_subtractor_1_s0[8]), .in_2(in_3));
  bit_divider bit_divider_1 (
    .in_1(in_1), .in_2(in_3), .Q7(bit_divider_1_r0[15]), .Q6(bit_divider_1_r0[14]),
    .Q5(bit_divider_1_r0[13]), .Q4(bit_divider_1_r0[12]), .Q3(bit_divider_1_r0[11]),
    .Q2(bit_divider_1_r0[10]), .Q1(bit_divider_1_r0[9]), .Q0(bit_divider_1_r0[8]), .R7(bit_divider_1_r0[7]),
    .R6(bit_divider_1_r0[6]), .R5(bit_divider_1_r0[5]), .R4(bit_divider_1_r0[4]), .R3(bit_divider_1_r0[3]),
    .R2(bit_divider_1_r0[2]), .R1(bit_divider_1_r0[1]), .R0(bit_divider_1_r0[0]));  // open: R8
  Multiplexer #(.select(2), .width(16)) multiplexer_1 (
    .in0({{7{1'b0}}, n8_bit_adder_1_out_4}), .in1({{7{1'b0}}, n8bit_subtractor_1_s0}),
    .in2(n8bit_multiplier_1_s0), .in3(bit_divider_1_r0), .out(multiplexer_1_out), .sel(in_2), .en(1'b1));
  hex_display hex_display_1 (
    .in_1(multiplexer_1_out[0]), .in_2(multiplexer_1_out[1]), .in_3(multiplexer_1_out[2]),
    .in_4(multiplexer_1_out[3]), .out_5(hex_display_1_out_5), .out_6(hex_display_1_out_6),
    .out_7(hex_display_1_out_7), .out_8(hex_display_1_out_8), .out_9(hex_display_1_out_9),
    .out_10(hex_display_1_out_10), .out_11(hex_display_1_out_11));
  hex_display hex_display_2 (
    .in_1(multiplexer_1_out[4]), .in_2(multiplexer_1_out[5]), .in_3(multiplexer_1_out[6]),
    .in_4(multiplexer_1_out[7]), .out_5(hex_display_2_out_5), .out_6(hex_display_2_out_6),
    .out_7(hex_display_2_out_7), .out_8(hex_display_2_out_8), .out_9(hex_display_2_out_9),
    .out_10(hex_display_2_out_10), .out_11(hex_display_2_out_11));
  hex_display hex_display_3 (
    .in_1(multiplexer_1_out[8]), .in_2(multiplexer_1_out[9]), .in_3(multiplexer_1_out[10]),
    .in_4(multiplexer_1_out[11]), .out_5(hex_display_3_out_5), .out_6(hex_display_3_out_6),
    .out_7(hex_display_3_out_7), .out_8(hex_display_3_out_8), .out_9(hex_display_3_out_9),
    .out_10(hex_display_3_out_10), .out_11(hex_display_3_out_11));
  hex_display hex_display_4 (
    .in_1(multiplexer_1_out[12]), .in_2(multiplexer_1_out[13]), .in_3(multiplexer_1_out[14]),
    .in_4(multiplexer_1_out[15]), .out_5(hex_display_4_out_5), .out_6(hex_display_4_out_6),
    .out_7(hex_display_4_out_7), .out_8(hex_display_4_out_8), .out_9(hex_display_4_out_9),
    .out_10(hex_display_4_out_10), .out_11(hex_display_4_out_11));
  _7_Segment_Display u_7_segment_display_1 (
    .g(hex_display_1_out_11), .f(hex_display_1_out_9), .a(hex_display_1_out_10), .b(hex_display_1_out_5),
    .e(hex_display_1_out_8), .d(hex_display_1_out_7), .c(hex_display_1_out_6));  // open: dp
  _7_Segment_Display u_7_segment_display_2 (
    .g(hex_display_2_out_11), .f(hex_display_2_out_9), .a(hex_display_2_out_10), .b(hex_display_2_out_5),
    .e(hex_display_2_out_8), .d(hex_display_2_out_7), .c(hex_display_2_out_6));  // open: dp
  _7_Segment_Display u_7_segment_display_3 (
    .g(hex_display_3_out_11), .f(hex_display_3_out_9), .a(hex_display_3_out_10), .b(hex_display_3_out_5),
    .e(hex_display_3_out_8), .d(hex_display_3_out_7), .c(hex_display_3_out_6));  // open: dp
  _7_Segment_Display u_7_segment_display_4 (
    .g(hex_display_4_out_11), .f(hex_display_4_out_9), .a(hex_display_4_out_10), .b(hex_display_4_out_5),
    .e(hex_display_4_out_8), .d(hex_display_4_out_7), .c(hex_display_4_out_6));  // open: dp

  // Other names for the same wires on the sheet: A0 = in_1[0]; A1 = in_1[1]; A2 = in_1[2]; A3 = in_1[3]; A4 = in_1[4];
  //   A5 = in_1[5]; A6 = in_1[6]; A7 = in_1[7]; B0 = in_3[0]; B1 = in_3[1]; B2 = in_3[2]; B3 = in_3[3]; B4 = in_3[4];
  //   B5 = in_3[5]; B6 = in_3[6]; B7 = in_3[7]

  // Notes on the sheet:
  //   8 BIT CALCULATOR
  //   NOTE:
  //   00-ADD,01_SUBTRACT,10-MULTIPLY,11-DIVISON
  //   For Divison first two gives quotient and last two remainder
  //   LSB
  //   remainder lsb
  //   remainder msb
  //   Quotient lsb
  //   MSB
  //   quotient msb
  //   FOR Subtraction if 1 negative , 0 positive
endmodule

module full_adder (
  input  Ai,
  input  Bi,
  input  Ci,
  output out_4,
  output out_5
);

  wire decoder_1_out1, decoder_1_out2, decoder_1_out3, decoder_1_out4, decoder_1_out5, decoder_1_out6,
       decoder_1_out7;

  Decoder #(.select(3)) decoder_1 (
    .out1(decoder_1_out1), .out2(decoder_1_out2), .out3(decoder_1_out3), .out4(decoder_1_out4),
    .out5(decoder_1_out5), .out6(decoder_1_out6), .out7(decoder_1_out7), .sel({Ci, Bi, Ai}), .en(1'b1));  // open: out0
  or sum (out_4, decoder_1_out1, decoder_1_out2, decoder_1_out4, decoder_1_out7);
  or carry (out_5, decoder_1_out3, decoder_1_out5, decoder_1_out6, decoder_1_out7);
endmodule

// A4
module _8_bit_adder (
  input  in_1,
  input  [7:0] in_2,
  input  [7:0] in_3,
  output out_4,
  output out_5,
  output out_6,
  output out_7,
  output out_8,
  output out_9,
  output out_10,
  output out_11,
  output out_12
);

  wire full_adder_1_out_5, full_adder_2_out_5, full_adder_3_out_5, full_adder_4_out_5, full_adder_5_out_5,
       full_adder_6_out_5, full_adder_7_out_5;

  full_adder full_adder_1 (.Ai(in_2[0]), .Bi(in_3[0]), .Ci(in_1), .out_4(out_4), .out_5(full_adder_1_out_5));
  full_adder full_adder_2 (
    .Ai(in_2[1]), .Bi(in_3[1]), .Ci(full_adder_1_out_5), .out_4(out_5), .out_5(full_adder_2_out_5));
  full_adder full_adder_3 (
    .Ai(in_2[2]), .Bi(in_3[2]), .Ci(full_adder_2_out_5), .out_4(out_6), .out_5(full_adder_3_out_5));
  full_adder full_adder_4 (
    .Ai(in_2[3]), .Bi(in_3[3]), .Ci(full_adder_3_out_5), .out_4(out_7), .out_5(full_adder_4_out_5));
  full_adder full_adder_5 (
    .Ai(in_2[4]), .Bi(in_3[4]), .Ci(full_adder_4_out_5), .out_4(out_8), .out_5(full_adder_5_out_5));
  full_adder full_adder_6 (
    .Ai(in_2[5]), .Bi(in_3[5]), .Ci(full_adder_5_out_5), .out_4(out_9), .out_5(full_adder_6_out_5));
  full_adder full_adder_7 (
    .Ai(in_2[6]), .Bi(in_3[6]), .Ci(full_adder_6_out_5), .out_4(out_10), .out_5(full_adder_7_out_5));
  full_adder full_adder_8 (.Ai(in_2[7]), .Bi(in_3[7]), .Ci(full_adder_7_out_5), .out_4(out_11), .out_5(out_12));

  // Other names for the same wires on the sheet: A0 = in_2[0]; A1 = in_2[1]; A2 = in_2[2]; A3 = in_2[3]; A4 = in_2[4];
  //   A5 = in_2[5]; A6 = in_2[6]; A7 = in_2[7]; B0 = in_3[0]; B1 = in_3[1]; B2 = in_3[2]; B3 = in_3[3]; B4 = in_3[4];
  //   B5 = in_3[5]; B6 = in_3[6]; B7 = in_3[7]
endmodule

module _8bit_subtractor (
  input  [7:0] in_1,
  input  [7:0] in_2,
  output S0,
  output S1,
  output S2,
  output S3,
  output S4,
  output S5,
  output S6,
  output S7,
  output _0_POSITIVE_1_NEGATIVE
);

  wire B0, B1, B2, B3, B4, B5, B6, B7, n8_bit_adder_1_out_4, n8_bit_adder_1_out_5, n8_bit_adder_1_out_6,
       n8_bit_adder_1_out_7, n8_bit_adder_1_out_8, n8_bit_adder_1_out_9, n8_bit_adder_1_out_10,
       n8_bit_adder_1_out_11, n8_bit_adder_1_out_12, not_2_out;
  wire [7:0] xor_1_out;

  _8_bit_adder u_8_bit_adder_1 (
    .out_4(n8_bit_adder_1_out_4), .in_2(in_1), .out_5(n8_bit_adder_1_out_5), .out_6(n8_bit_adder_1_out_6),
    .out_7(n8_bit_adder_1_out_7), .out_8(n8_bit_adder_1_out_8), .in_3({B7, B6, B5, B4, B3, B2, B1, B0}),
    .out_9(n8_bit_adder_1_out_9), .out_10(n8_bit_adder_1_out_10), .out_11(n8_bit_adder_1_out_11),
    .out_12(n8_bit_adder_1_out_12), .in_1(1'b0));
  not not_1 (_0_POSITIVE_1_NEGATIVE, n8_bit_adder_1_out_12);
  xor xor_1 (xor_1_out[0], n8_bit_adder_1_out_4, _0_POSITIVE_1_NEGATIVE);
  xor xor_2 (xor_1_out[1], n8_bit_adder_1_out_5, _0_POSITIVE_1_NEGATIVE);
  xor xor_3 (xor_1_out[2], n8_bit_adder_1_out_6, _0_POSITIVE_1_NEGATIVE);
  xor xor_4 (xor_1_out[3], n8_bit_adder_1_out_7, _0_POSITIVE_1_NEGATIVE);
  xor xor_5 (xor_1_out[4], n8_bit_adder_1_out_8, _0_POSITIVE_1_NEGATIVE);
  xor xor_6 (xor_1_out[5], n8_bit_adder_1_out_9, _0_POSITIVE_1_NEGATIVE);
  xor xor_7 (xor_1_out[6], n8_bit_adder_1_out_10, _0_POSITIVE_1_NEGATIVE);
  xor xor_8 (xor_1_out[7], n8_bit_adder_1_out_11, _0_POSITIVE_1_NEGATIVE);
  not not_2 (not_2_out, _0_POSITIVE_1_NEGATIVE);
  _8_bit_adder u_8_bit_adder_2 (
    .out_4(S0), .in_2(xor_1_out), .out_5(S1), .out_6(S2), .out_7(S3), .out_8(S4), .in_3({8{1'b0}}),
    .out_9(S5), .out_10(S6), .out_11(S7), .in_1(not_2_out));  // open: out_12
  xor xor_9 (B0, in_2[0], 1'b1);
  xor xor_10 (B1, in_2[1], 1'b1);
  xor xor_11 (B2, in_2[2], 1'b1);
  xor xor_12 (B3, in_2[3], 1'b1);
  xor xor_13 (B4, in_2[4], 1'b1);
  xor xor_14 (B5, in_2[5], 1'b1);
  xor xor_15 (B6, 1'b1, in_2[6]);
  xor xor_16 (B7, 1'b1, in_2[7]);

  // Other names for the same wires on the sheet: A0 = in_1[0]; A1 = in_1[1]; A2 = in_1[2]; A3 = in_1[3]; A4 = in_1[4];
  //   A5 = in_1[5]; A6 = in_1[6]; A7 = in_1[7]
endmodule

module _8BIT_MULTIPLIER (
  input  [7:0] in_1,
  input  [7:0] in_2,
  output S3,
  output S2,
  output S1,
  output S0,
  output S15,
  output S14,
  output S13,
  output S12,
  output S11,
  output S10,
  output S9,
  output S8,
  output S7,
  output S6,
  output S5,
  output S4
);

  wire [6:0] A1B0_out;
  wire [7:0] A0B1_out, A0B2_out, A0B3_out, A0B4_out, A0B5_out, A0B6_out, A0B7_out, n8_bit_adder_1_out_5,
       n8_bit_adder_3_out_5, n8_bit_adder_4_out_5, n8_bit_adder_5_out_5, n8_bit_adder_6_out_5,
       n8_bit_adder_7_out_5;

  and A7B7 (A0B7_out[7], in_1[7], in_2[7]);
  and A7B6 (A0B6_out[7], in_1[7], in_2[6]);
  and A5B7 (A0B7_out[5], in_1[5], in_2[7]);
  and A6B7 (A0B7_out[6], in_1[6], in_2[7]);
  and A7B5 (A0B5_out[7], in_1[7], in_2[5]);
  and A6B6 (A0B6_out[6], in_1[6], in_2[6]);
  and A5B6 (A0B6_out[5], in_1[5], in_2[6]);
  and A3B7 (A0B7_out[3], in_1[3], in_2[7]);
  and A4B7 (A0B7_out[4], in_1[4], in_2[7]);
  and A7B4 (A0B4_out[7], in_1[7], in_2[4]);
  and A6B4 (A0B4_out[6], in_1[6], in_2[4]);
  and A6B5 (A0B5_out[6], in_1[6], in_2[5]);
  and A5B5 (A0B5_out[5], in_1[5], in_2[5]);
  and A3B6 (A0B6_out[3], in_1[3], in_2[6]);
  and A4B6 (A0B6_out[4], in_1[4], in_2[6]);
  and A1B7 (A0B7_out[1], in_1[1], in_2[7]);
  and A2B7 (A0B7_out[2], in_1[2], in_2[7]);
  and A6B1 (A0B1_out[6], in_1[6], in_2[1]);
  and A7B1 (A0B1_out[7], in_1[7], in_2[1]);
  and A7B3 (A0B3_out[7], in_1[7], in_2[3]);
  and A6B3 (A0B3_out[6], in_1[6], in_2[3]);
  and A5B4 (A0B4_out[5], in_1[5], in_2[4]);
  and A4B4 (A0B4_out[4], in_1[4], in_2[4]);
  and A3B5 (A0B5_out[3], in_1[3], in_2[5]);
  and A4B5 (A0B5_out[4], in_1[4], in_2[5]);
  and A2B6 (A0B6_out[2], in_1[2], in_2[6]);
  and A1B6 (A0B6_out[1], in_1[1], in_2[6]);
  and A0B7 (A0B7_out[0], in_1[0], in_2[7]);
  and A4B1 (A0B1_out[4], in_1[4], in_2[1]);
  and A5B1 (A0B1_out[5], in_1[5], in_2[1]);
  and A7B2 (A0B2_out[7], in_1[7], in_2[2]);
  and A6B2 (A0B2_out[6], in_1[6], in_2[2]);
  and A5B3 (A0B3_out[5], in_1[5], in_2[3]);
  and A4B3 (A0B3_out[4], in_1[4], in_2[3]);
  and A2B4 (A0B4_out[2], in_1[2], in_2[4]);
  and A3B4 (A0B4_out[3], in_1[3], in_2[4]);
  and A1B5 (A0B5_out[1], in_1[1], in_2[5]);
  and A2B5 (A0B5_out[2], in_1[2], in_2[5]);
  and A0B6 (A0B6_out[0], in_1[0], in_2[6]);
  and A2B1 (A0B1_out[2], in_1[2], in_2[1]);
  and A3B1 (A0B1_out[3], in_1[3], in_2[1]);
  and A5B2 (A0B2_out[5], in_1[5], in_2[2]);
  and A4B2 (A0B2_out[4], in_1[4], in_2[2]);
  and A2B3 (A0B3_out[2], in_1[2], in_2[3]);
  and A3B3 (A0B3_out[3], in_1[3], in_2[3]);
  and A1B4 (A0B4_out[1], in_1[1], in_2[4]);
  buf A0B5 (A0B5_out[0], in_2[5]);  // AND_Gate
  _8_bit_adder u_8_bit_adder_1 (
    .out_4(S6), .in_2(n8_bit_adder_3_out_5), .out_5(n8_bit_adder_1_out_5[0]),
    .out_6(n8_bit_adder_1_out_5[1]), .out_7(n8_bit_adder_1_out_5[2]), .out_8(n8_bit_adder_1_out_5[3]),
    .in_3(A0B6_out), .out_9(n8_bit_adder_1_out_5[4]), .out_10(n8_bit_adder_1_out_5[5]),
    .out_11(n8_bit_adder_1_out_5[6]), .out_12(n8_bit_adder_1_out_5[7]), .in_1(1'b0));
  _8_bit_adder u_8_bit_adder_2 (
    .out_4(S7), .in_2(n8_bit_adder_1_out_5), .out_5(S8), .out_6(S9), .out_7(S10), .out_8(S11),
    .in_3(A0B7_out), .out_9(S12), .out_10(S13), .out_11(S14), .out_12(S15), .in_1(1'b0));
  and A1B1 (A0B1_out[1], in_1[1], in_2[1]);
  and A0B1 (A0B1_out[0], in_1[0], in_2[1]);
  and A3B2 (A0B2_out[3], in_1[3], in_2[2]);
  and A2B2 (A0B2_out[2], in_1[2], in_2[2]);
  and A1B3 (A0B3_out[1], in_1[1], in_2[3]);
  and A0B4 (A0B4_out[0], in_1[0], in_2[4]);
  _8_bit_adder u_8_bit_adder_3 (
    .out_4(S5), .in_2(n8_bit_adder_4_out_5), .out_5(n8_bit_adder_3_out_5[0]),
    .out_6(n8_bit_adder_3_out_5[1]), .out_7(n8_bit_adder_3_out_5[2]), .out_8(n8_bit_adder_3_out_5[3]),
    .in_3(A0B5_out), .out_9(n8_bit_adder_3_out_5[4]), .out_10(n8_bit_adder_3_out_5[5]),
    .out_11(n8_bit_adder_3_out_5[6]), .out_12(n8_bit_adder_3_out_5[7]), .in_1(1'b0));
  and A7B0 (A1B0_out[6], in_1[7], in_2[0]);
  and A1B2 (A0B2_out[1], in_1[1], in_2[2]);
  and A0B2 (A0B2_out[0], in_1[0], in_2[2]);
  and A0B3 (A0B3_out[0], in_1[0], in_2[3]);
  _8_bit_adder u_8_bit_adder_4 (
    .out_4(S4), .in_2(n8_bit_adder_5_out_5), .out_5(n8_bit_adder_4_out_5[0]),
    .out_6(n8_bit_adder_4_out_5[1]), .out_7(n8_bit_adder_4_out_5[2]), .out_8(n8_bit_adder_4_out_5[3]),
    .in_3(A0B4_out), .out_9(n8_bit_adder_4_out_5[4]), .out_10(n8_bit_adder_4_out_5[5]),
    .out_11(n8_bit_adder_4_out_5[6]), .out_12(n8_bit_adder_4_out_5[7]), .in_1(1'b0));
  and A5B0 (A1B0_out[4], in_1[5], in_2[0]);
  and A6B0 (A1B0_out[5], in_1[6], in_2[0]);
  _8_bit_adder u_8_bit_adder_5 (
    .out_4(S3), .in_2(n8_bit_adder_6_out_5), .out_5(n8_bit_adder_5_out_5[0]),
    .out_6(n8_bit_adder_5_out_5[1]), .out_7(n8_bit_adder_5_out_5[2]), .out_8(n8_bit_adder_5_out_5[3]),
    .in_3(A0B3_out), .out_9(n8_bit_adder_5_out_5[4]), .out_10(n8_bit_adder_5_out_5[5]),
    .out_11(n8_bit_adder_5_out_5[6]), .out_12(n8_bit_adder_5_out_5[7]), .in_1(1'b0));
  and A3B0 (A1B0_out[2], in_1[3], in_2[0]);
  and A4B0 (A1B0_out[3], in_1[4], in_2[0]);
  _8_bit_adder u_8_bit_adder_6 (
    .out_4(S2), .in_2(n8_bit_adder_7_out_5), .out_5(n8_bit_adder_6_out_5[0]),
    .out_6(n8_bit_adder_6_out_5[1]), .out_7(n8_bit_adder_6_out_5[2]), .out_8(n8_bit_adder_6_out_5[3]),
    .in_3(A0B2_out), .out_9(n8_bit_adder_6_out_5[4]), .out_10(n8_bit_adder_6_out_5[5]),
    .out_11(n8_bit_adder_6_out_5[6]), .out_12(n8_bit_adder_6_out_5[7]), .in_1(1'b0));
  and A2B0 (A1B0_out[1], in_1[2], in_2[0]);
  and A1B0 (A1B0_out[0], in_1[1], in_2[0]);
  _8_bit_adder u_8_bit_adder_7 (
    .out_4(S1), .in_2({1'b0, A1B0_out}), .out_5(n8_bit_adder_7_out_5[0]), .out_6(n8_bit_adder_7_out_5[1]),
    .out_7(n8_bit_adder_7_out_5[2]), .out_8(n8_bit_adder_7_out_5[3]), .in_3(A0B1_out),
    .out_9(n8_bit_adder_7_out_5[4]), .out_10(n8_bit_adder_7_out_5[5]), .out_11(n8_bit_adder_7_out_5[6]),
    .out_12(n8_bit_adder_7_out_5[7]), .in_1(1'b0));
  and A0B0 (S0, in_1[0], in_2[0]);

  // Other names for the same wires on the sheet: A0 = in_1[0]; A1 = in_1[1]; A2 = in_1[2]; A3 = in_1[3]; A4 = in_1[4];
  //   A5 = in_1[5]; A6 = in_1[6]; A7 = in_1[7]; B0 = in_2[0]; B1 = in_2[1]; B2 = in_2[2]; B3 = in_2[3]; B4 = in_2[4];
  //   B5 = in_2[5]; B6 = in_2[6]; B7 = in_2[7]
endmodule

module bit_divider (
  input  [7:0] in_1,
  input  [7:0] in_2,
  output R8,
  output R7,
  output R6,
  output R5,
  output R4,
  output R3,
  output R2,
  output R1,
  output R0,
  output Q7,
  output Q6,
  output Q5,
  output Q4,
  output Q3,
  output Q2,
  output Q1,
  output Q0
);

  wire controled_subtract_mulyiplex_2_bo, controled_subtract_mulyiplex_2_d,
       controled_subtract_mulyiplex_4_bo, controled_subtract_mulyiplex_4_d,
       controled_subtract_mulyiplex_5_bo, controled_subtract_mulyiplex_5_d,
       controled_subtract_mulyiplex_7_bo, controled_subtract_mulyiplex_7_d,
       controled_subtract_mulyiplex_8_bo, controled_subtract_mulyiplex_8_d,
       controled_subtract_mulyiplex_9_bo, controled_subtract_mulyiplex_9_d,
       controled_subtract_mulyiplex_11_bo, controled_subtract_mulyiplex_11_d,
       controled_subtract_mulyiplex_12_bo, controled_subtract_mulyiplex_12_d,
       controled_subtract_mulyiplex_13_bo, controled_subtract_mulyiplex_13_d,
       controled_subtract_mulyiplex_14_bo, controled_subtract_mulyiplex_14_d,
       controled_subtract_mulyiplex_16_bo, controled_subtract_mulyiplex_16_d,
       controled_subtract_mulyiplex_17_bo, controled_subtract_mulyiplex_17_d,
       controled_subtract_mulyiplex_18_bo, controled_subtract_mulyiplex_18_d,
       controled_subtract_mulyiplex_20_bo, controled_subtract_mulyiplex_20_d,
       controled_subtract_mulyiplex_21_bo, controled_subtract_mulyiplex_21_d,
       controled_subtract_mulyiplex_22_bo, controled_subtract_mulyiplex_22_d,
       controled_subtract_mulyiplex_23_bo, controled_subtract_mulyiplex_23_d,
       controled_subtract_mulyiplex_25_bo, controled_subtract_mulyiplex_25_d,
       controled_subtract_mulyiplex_26_bo, controled_subtract_mulyiplex_26_d,
       controled_subtract_mulyiplex_27_bo, controled_subtract_mulyiplex_27_d,
       controled_subtract_mulyiplex_28_bo, controled_subtract_mulyiplex_28_d,
       controled_subtract_mulyiplex_29_bo, controled_subtract_mulyiplex_29_d,
       controled_subtract_mulyiplex_31_bo, controled_subtract_mulyiplex_31_d,
       controled_subtract_mulyiplex_32_bo, controled_subtract_mulyiplex_32_d,
       controled_subtract_mulyiplex_33_bo, controled_subtract_mulyiplex_33_d,
       controled_subtract_mulyiplex_34_bo, controled_subtract_mulyiplex_34_d,
       controled_subtract_mulyiplex_35_bo, controled_subtract_mulyiplex_35_d,
       controled_subtract_mulyiplex_36_bo, controled_subtract_mulyiplex_36_d,
       controled_subtract_mulyiplex_37_bo, controled_subtract_mulyiplex_37_d,
       controled_subtract_mulyiplex_38_bo, controled_subtract_mulyiplex_38_d,
       controled_subtract_mulyiplex_39_bo, controled_subtract_mulyiplex_39_d,
       controled_subtract_mulyiplex_40_bo, controled_subtract_mulyiplex_40_d,
       controled_subtract_mulyiplex_41_bo, controled_subtract_mulyiplex_41_d,
       controled_subtract_mulyiplex_42_bo, controled_subtract_mulyiplex_42_d,
       controled_subtract_mulyiplex_43_bo, controled_subtract_mulyiplex_43_d,
       controled_subtract_mulyiplex_44_bo, controled_subtract_mulyiplex_45_bo,
       controled_subtract_mulyiplex_45_d, controled_subtract_mulyiplex_46_bo,
       controled_subtract_mulyiplex_46_d, controled_subtract_mulyiplex_47_bo,
       controled_subtract_mulyiplex_47_d, controled_subtract_mulyiplex_48_bo,
       controled_subtract_mulyiplex_48_d, controled_subtract_mulyiplex_49_bo,
       controled_subtract_mulyiplex_49_d, controled_subtract_mulyiplex_50_bo,
       controled_subtract_mulyiplex_51_bo, controled_subtract_mulyiplex_51_d,
       controled_subtract_mulyiplex_52_bo, controled_subtract_mulyiplex_52_d,
       controled_subtract_mulyiplex_53_bo, controled_subtract_mulyiplex_53_d,
       controled_subtract_mulyiplex_54_bo, controled_subtract_mulyiplex_54_d,
       controled_subtract_mulyiplex_55_bo, controled_subtract_mulyiplex_56_bo,
       controled_subtract_mulyiplex_56_d, controled_subtract_mulyiplex_57_bo,
       controled_subtract_mulyiplex_57_d, controled_subtract_mulyiplex_58_bo,
       controled_subtract_mulyiplex_58_d, controled_subtract_mulyiplex_59_bo,
       controled_subtract_mulyiplex_60_bo, controled_subtract_mulyiplex_60_d,
       controled_subtract_mulyiplex_61_bo, controled_subtract_mulyiplex_61_d,
       controled_subtract_mulyiplex_62_bo, controled_subtract_mulyiplex_62_d,
       controled_subtract_mulyiplex_63_bo, controled_subtract_mulyiplex_63_d,
       controled_subtract_mulyiplex_64_bo, controled_subtract_mulyiplex_64_d,
       controled_subtract_mulyiplex_65_bo, controled_subtract_mulyiplex_65_d,
       controled_subtract_mulyiplex_66_bo, controled_subtract_mulyiplex_67_bo,
       controled_subtract_mulyiplex_67_d, controled_subtract_mulyiplex_68_bo,
       controled_subtract_mulyiplex_68_d, controled_subtract_mulyiplex_69_bo,
       controled_subtract_mulyiplex_70_bo, controled_subtract_mulyiplex_70_d,
       controled_subtract_mulyiplex_71_bo, controled_subtract_mulyiplex_72_bo, OS0, OS1, OS2, OS3, OS4, OS5,
       OS6, OS7;

  not not_1 (Q7, OS0);
  controled_subtract_mulyiplex controled_subtract_mulyiplex_1 (
    .x(1'b0), .y(1'b0), .os(OS0), .bi(controled_subtract_mulyiplex_2_bo), .bo(OS0));  // open: d
  not not_2 (Q6, OS1);
  not not_3 (Q5, OS2);
  controled_subtract_mulyiplex controled_subtract_mulyiplex_2 (
    .x(1'b0), .y(in_2[7]), .os(OS0), .bi(controled_subtract_mulyiplex_4_bo),
    .d(controled_subtract_mulyiplex_2_d), .bo(controled_subtract_mulyiplex_2_bo));
  controled_subtract_mulyiplex controled_subtract_mulyiplex_3 (
    .x(controled_subtract_mulyiplex_2_d), .y(1'b0), .os(OS1), .bi(controled_subtract_mulyiplex_5_bo), .bo(OS1));  // open: d
  not not_4 (Q4, OS3);
  controled_subtract_mulyiplex controled_subtract_mulyiplex_4 (
    .x(1'b0), .y(in_2[6]), .os(OS0), .bi(controled_subtract_mulyiplex_7_bo),
    .d(controled_subtract_mulyiplex_4_d), .bo(controled_subtract_mulyiplex_4_bo));
  controled_subtract_mulyiplex controled_subtract_mulyiplex_5 (
    .x(controled_subtract_mulyiplex_4_d), .y(in_2[7]), .os(OS1), .bi(controled_subtract_mulyiplex_8_bo),
    .d(controled_subtract_mulyiplex_5_d), .bo(controled_subtract_mulyiplex_5_bo));
  controled_subtract_mulyiplex controled_subtract_mulyiplex_6 (
    .x(controled_subtract_mulyiplex_5_d), .y(1'b0), .os(OS2), .bi(controled_subtract_mulyiplex_9_bo), .bo(OS2));  // open: d
  not not_5 (Q3, OS4);
  controled_subtract_mulyiplex controled_subtract_mulyiplex_7 (
    .x(1'b0), .y(in_2[5]), .os(OS0), .bi(controled_subtract_mulyiplex_11_bo),
    .d(controled_subtract_mulyiplex_7_d), .bo(controled_subtract_mulyiplex_7_bo));
  controled_subtract_mulyiplex controled_subtract_mulyiplex_8 (
    .x(controled_subtract_mulyiplex_7_d), .y(in_2[6]), .os(OS1), .bi(controled_subtract_mulyiplex_12_bo),
    .d(controled_subtract_mulyiplex_8_d), .bo(controled_subtract_mulyiplex_8_bo));
  controled_subtract_mulyiplex controled_subtract_mulyiplex_9 (
    .x(controled_subtract_mulyiplex_8_d), .y(in_2[7]), .os(OS2), .bi(controled_subtract_mulyiplex_13_bo),
    .d(controled_subtract_mulyiplex_9_d), .bo(controled_subtract_mulyiplex_9_bo));
  controled_subtract_mulyiplex controled_subtract_mulyiplex_10 (
    .x(controled_subtract_mulyiplex_9_d), .y(1'b0), .os(OS3), .bi(controled_subtract_mulyiplex_14_bo),
    .bo(OS3));  // open: d
  not not_6 (Q2, OS5);
  controled_subtract_mulyiplex controled_subtract_mulyiplex_11 (
    .x(1'b0), .y(in_2[4]), .os(OS0), .bi(controled_subtract_mulyiplex_20_bo),
    .d(controled_subtract_mulyiplex_11_d), .bo(controled_subtract_mulyiplex_11_bo));
  controled_subtract_mulyiplex controled_subtract_mulyiplex_12 (
    .x(controled_subtract_mulyiplex_11_d), .y(in_2[5]), .os(OS1), .bi(controled_subtract_mulyiplex_21_bo),
    .d(controled_subtract_mulyiplex_12_d), .bo(controled_subtract_mulyiplex_12_bo));
  controled_subtract_mulyiplex controled_subtract_mulyiplex_13 (
    .x(controled_subtract_mulyiplex_12_d), .y(in_2[6]), .os(OS2), .bi(controled_subtract_mulyiplex_16_bo),
    .d(controled_subtract_mulyiplex_13_d), .bo(controled_subtract_mulyiplex_13_bo));
  controled_subtract_mulyiplex controled_subtract_mulyiplex_14 (
    .x(controled_subtract_mulyiplex_13_d), .y(in_2[7]), .os(OS3), .bi(controled_subtract_mulyiplex_17_bo),
    .d(controled_subtract_mulyiplex_14_d), .bo(controled_subtract_mulyiplex_14_bo));
  controled_subtract_mulyiplex controled_subtract_mulyiplex_15 (
    .x(controled_subtract_mulyiplex_14_d), .y(1'b0), .os(OS4), .bi(controled_subtract_mulyiplex_18_bo),
    .bo(OS4));  // open: d
  not not_7 (Q1, OS6);
  controled_subtract_mulyiplex controled_subtract_mulyiplex_16 (
    .x(controled_subtract_mulyiplex_21_d), .y(in_2[5]), .os(OS2), .bi(controled_subtract_mulyiplex_27_bo),
    .d(controled_subtract_mulyiplex_16_d), .bo(controled_subtract_mulyiplex_16_bo));
  controled_subtract_mulyiplex controled_subtract_mulyiplex_17 (
    .x(controled_subtract_mulyiplex_16_d), .y(in_2[6]), .os(OS3), .bi(controled_subtract_mulyiplex_28_bo),
    .d(controled_subtract_mulyiplex_17_d), .bo(controled_subtract_mulyiplex_17_bo));
  controled_subtract_mulyiplex controled_subtract_mulyiplex_18 (
    .x(controled_subtract_mulyiplex_17_d), .y(in_2[7]), .os(OS4), .bi(controled_subtract_mulyiplex_22_bo),
    .d(controled_subtract_mulyiplex_18_d), .bo(controled_subtract_mulyiplex_18_bo));
  controled_subtract_mulyiplex controled_subtract_mulyiplex_19 (
    .x(controled_subtract_mulyiplex_18_d), .y(1'b0), .os(OS5), .bi(controled_subtract_mulyiplex_23_bo),
    .bo(OS5));  // open: d
  controled_subtract_mulyiplex controled_subtract_mulyiplex_20 (
    .x(1'b0), .y(in_2[3]), .os(OS0), .bi(controled_subtract_mulyiplex_25_bo),
    .d(controled_subtract_mulyiplex_20_d), .bo(controled_subtract_mulyiplex_20_bo));
  controled_subtract_mulyiplex controled_subtract_mulyiplex_21 (
    .x(controled_subtract_mulyiplex_20_d), .y(in_2[4]), .os(OS1), .bi(controled_subtract_mulyiplex_26_bo),
    .d(controled_subtract_mulyiplex_21_d), .bo(controled_subtract_mulyiplex_21_bo));
  controled_subtract_mulyiplex controled_subtract_mulyiplex_22 (
    .x(controled_subtract_mulyiplex_28_d), .y(in_2[6]), .os(OS4), .bi(controled_subtract_mulyiplex_35_bo),
    .d(controled_subtract_mulyiplex_22_d), .bo(controled_subtract_mulyiplex_22_bo));
  controled_subtract_mulyiplex controled_subtract_mulyiplex_23 (
    .x(controled_subtract_mulyiplex_22_d), .y(in_2[7]), .os(OS5), .bi(controled_subtract_mulyiplex_36_bo),
    .d(controled_subtract_mulyiplex_23_d), .bo(controled_subtract_mulyiplex_23_bo));
  controled_subtract_mulyiplex controled_subtract_mulyiplex_24 (
    .x(controled_subtract_mulyiplex_23_d), .y(1'b0), .os(OS6), .bi(controled_subtract_mulyiplex_29_bo),
    .bo(OS6));  // open: d
  not not_8 (Q0, OS7);
  controled_subtract_mulyiplex controled_subtract_mulyiplex_25 (
    .x(1'b0), .y(in_2[2]), .os(OS0), .bi(controled_subtract_mulyiplex_31_bo),
    .d(controled_subtract_mulyiplex_25_d), .bo(controled_subtract_mulyiplex_25_bo));
  controled_subtract_mulyiplex controled_subtract_mulyiplex_26 (
    .x(controled_subtract_mulyiplex_25_d), .y(in_2[3]), .os(OS1), .bi(controled_subtract_mulyiplex_32_bo),
    .d(controled_subtract_mulyiplex_26_d), .bo(controled_subtract_mulyiplex_26_bo));
  controled_subtract_mulyiplex controled_subtract_mulyiplex_27 (
    .x(controled_subtract_mulyiplex_26_d), .y(in_2[4]), .os(OS2), .bi(controled_subtract_mulyiplex_33_bo),
    .d(controled_subtract_mulyiplex_27_d), .bo(controled_subtract_mulyiplex_27_bo));
  controled_subtract_mulyiplex controled_subtract_mulyiplex_28 (
    .x(controled_subtract_mulyiplex_27_d), .y(in_2[5]), .os(OS3), .bi(controled_subtract_mulyiplex_34_bo),
    .d(controled_subtract_mulyiplex_28_d), .bo(controled_subtract_mulyiplex_28_bo));
  controled_subtract_mulyiplex controled_subtract_mulyiplex_29 (
    .x(controled_subtract_mulyiplex_36_d), .y(in_2[7]), .os(OS6), .bi(controled_subtract_mulyiplex_43_bo),
    .d(controled_subtract_mulyiplex_29_d), .bo(controled_subtract_mulyiplex_29_bo));
  controled_subtract_mulyiplex controled_subtract_mulyiplex_30 (
    .x(controled_subtract_mulyiplex_29_d), .y(1'b0), .os(OS7), .bi(controled_subtract_mulyiplex_44_bo),
    .d(R8), .bo(OS7));
  controled_subtract_mulyiplex controled_subtract_mulyiplex_31 (
    .x(1'b0), .y(in_2[1]), .os(OS0), .bi(controled_subtract_mulyiplex_37_bo),
    .d(controled_subtract_mulyiplex_31_d), .bo(controled_subtract_mulyiplex_31_bo));
  controled_subtract_mulyiplex controled_subtract_mulyiplex_32 (
    .x(controled_subtract_mulyiplex_31_d), .y(in_2[2]), .os(OS1), .bi(controled_subtract_mulyiplex_38_bo),
    .d(controled_subtract_mulyiplex_32_d), .bo(controled_subtract_mulyiplex_32_bo));
  controled_subtract_mulyiplex controled_subtract_mulyiplex_33 (
    .x(controled_subtract_mulyiplex_32_d), .y(in_2[3]), .os(OS2), .bi(controled_subtract_mulyiplex_39_bo),
    .d(controled_subtract_mulyiplex_33_d), .bo(controled_subtract_mulyiplex_33_bo));
  controled_subtract_mulyiplex controled_subtract_mulyiplex_34 (
    .x(controled_subtract_mulyiplex_33_d), .y(in_2[4]), .os(OS3), .bi(controled_subtract_mulyiplex_40_bo),
    .d(controled_subtract_mulyiplex_34_d), .bo(controled_subtract_mulyiplex_34_bo));
  controled_subtract_mulyiplex controled_subtract_mulyiplex_35 (
    .x(controled_subtract_mulyiplex_34_d), .y(in_2[5]), .os(OS4), .bi(controled_subtract_mulyiplex_41_bo),
    .d(controled_subtract_mulyiplex_35_d), .bo(controled_subtract_mulyiplex_35_bo));
  controled_subtract_mulyiplex controled_subtract_mulyiplex_36 (
    .x(controled_subtract_mulyiplex_35_d), .y(in_2[6]), .os(OS5), .bi(controled_subtract_mulyiplex_42_bo),
    .d(controled_subtract_mulyiplex_36_d), .bo(controled_subtract_mulyiplex_36_bo));
  controled_subtract_mulyiplex controled_subtract_mulyiplex_37 (
    .x(in_1[7]), .y(in_2[0]), .os(OS0), .bi(1'b0), .d(controled_subtract_mulyiplex_37_d),
    .bo(controled_subtract_mulyiplex_37_bo));
  controled_subtract_mulyiplex controled_subtract_mulyiplex_38 (
    .x(controled_subtract_mulyiplex_37_d), .y(in_2[1]), .os(OS1), .bi(controled_subtract_mulyiplex_51_bo),
    .d(controled_subtract_mulyiplex_38_d), .bo(controled_subtract_mulyiplex_38_bo));
  controled_subtract_mulyiplex controled_subtract_mulyiplex_39 (
    .x(controled_subtract_mulyiplex_38_d), .y(in_2[2]), .os(OS2), .bi(controled_subtract_mulyiplex_45_bo),
    .d(controled_subtract_mulyiplex_39_d), .bo(controled_subtract_mulyiplex_39_bo));
  controled_subtract_mulyiplex controled_subtract_mulyiplex_40 (
    .x(controled_subtract_mulyiplex_39_d), .y(in_2[3]), .os(OS3), .bi(controled_subtract_mulyiplex_46_bo),
    .d(controled_subtract_mulyiplex_40_d), .bo(controled_subtract_mulyiplex_40_bo));
  controled_subtract_mulyiplex controled_subtract_mulyiplex_41 (
    .x(controled_subtract_mulyiplex_40_d), .y(in_2[4]), .os(OS4), .bi(controled_subtract_mulyiplex_47_bo),
    .d(controled_subtract_mulyiplex_41_d), .bo(controled_subtract_mulyiplex_41_bo));
  controled_subtract_mulyiplex controled_subtract_mulyiplex_42 (
    .x(controled_subtract_mulyiplex_41_d), .y(in_2[5]), .os(OS5), .bi(controled_subtract_mulyiplex_48_bo),
    .d(controled_subtract_mulyiplex_42_d), .bo(controled_subtract_mulyiplex_42_bo));
  controled_subtract_mulyiplex controled_subtract_mulyiplex_43 (
    .x(controled_subtract_mulyiplex_42_d), .y(in_2[6]), .os(OS6), .bi(controled_subtract_mulyiplex_49_bo),
    .d(controled_subtract_mulyiplex_43_d), .bo(controled_subtract_mulyiplex_43_bo));
  controled_subtract_mulyiplex controled_subtract_mulyiplex_44 (
    .x(controled_subtract_mulyiplex_43_d), .y(in_2[7]), .os(OS7), .bi(controled_subtract_mulyiplex_50_bo),
    .d(R7), .bo(controled_subtract_mulyiplex_44_bo));
  controled_subtract_mulyiplex controled_subtract_mulyiplex_45 (
    .x(controled_subtract_mulyiplex_51_d), .y(in_2[1]), .os(OS2), .bi(controled_subtract_mulyiplex_56_bo),
    .d(controled_subtract_mulyiplex_45_d), .bo(controled_subtract_mulyiplex_45_bo));
  controled_subtract_mulyiplex controled_subtract_mulyiplex_46 (
    .x(controled_subtract_mulyiplex_45_d), .y(in_2[2]), .os(OS3), .bi(controled_subtract_mulyiplex_57_bo),
    .d(controled_subtract_mulyiplex_46_d), .bo(controled_subtract_mulyiplex_46_bo));
  controled_subtract_mulyiplex controled_subtract_mulyiplex_47 (
    .x(controled_subtract_mulyiplex_46_d), .y(in_2[3]), .os(OS4), .bi(controled_subtract_mulyiplex_52_bo),
    .d(controled_subtract_mulyiplex_47_d), .bo(controled_subtract_mulyiplex_47_bo));
  controled_subtract_mulyiplex controled_subtract_mulyiplex_48 (
    .x(controled_subtract_mulyiplex_47_d), .y(in_2[4]), .os(OS5), .bi(controled_subtract_mulyiplex_53_bo),
    .d(controled_subtract_mulyiplex_48_d), .bo(controled_subtract_mulyiplex_48_bo));
  controled_subtract_mulyiplex controled_subtract_mulyiplex_49 (
    .x(controled_subtract_mulyiplex_48_d), .y(in_2[5]), .os(OS6), .bi(controled_subtract_mulyiplex_54_bo),
    .d(controled_subtract_mulyiplex_49_d), .bo(controled_subtract_mulyiplex_49_bo));
  controled_subtract_mulyiplex controled_subtract_mulyiplex_50 (
    .x(controled_subtract_mulyiplex_49_d), .y(in_2[6]), .os(OS7), .bi(controled_subtract_mulyiplex_55_bo),
    .d(R6), .bo(controled_subtract_mulyiplex_50_bo));
  controled_subtract_mulyiplex controled_subtract_mulyiplex_51 (
    .x(in_1[6]), .y(in_2[0]), .os(OS1), .bi(1'b0), .d(controled_subtract_mulyiplex_51_d),
    .bo(controled_subtract_mulyiplex_51_bo));
  controled_subtract_mulyiplex controled_subtract_mulyiplex_52 (
    .x(controled_subtract_mulyiplex_57_d), .y(in_2[2]), .os(OS4), .bi(controled_subtract_mulyiplex_61_bo),
    .d(controled_subtract_mulyiplex_52_d), .bo(controled_subtract_mulyiplex_52_bo));
  controled_subtract_mulyiplex controled_subtract_mulyiplex_53 (
    .x(controled_subtract_mulyiplex_52_d), .y(in_2[3]), .os(OS5), .bi(controled_subtract_mulyiplex_62_bo),
    .d(controled_subtract_mulyiplex_53_d), .bo(controled_subtract_mulyiplex_53_bo));
  controled_subtract_mulyiplex controled_subtract_mulyiplex_54 (
    .x(controled_subtract_mulyiplex_53_d), .y(in_2[4]), .os(OS6), .bi(controled_subtract_mulyiplex_58_bo),
    .d(controled_subtract_mulyiplex_54_d), .bo(controled_subtract_mulyiplex_54_bo));
  controled_subtract_mulyiplex controled_subtract_mulyiplex_55 (
    .x(controled_subtract_mulyiplex_54_d), .y(in_2[5]), .os(OS7), .bi(controled_subtract_mulyiplex_59_bo),
    .d(R5), .bo(controled_subtract_mulyiplex_55_bo));
  controled_subtract_mulyiplex controled_subtract_mulyiplex_56 (
    .x(in_1[5]), .y(in_2[0]), .os(OS2), .bi(1'b0), .d(controled_subtract_mulyiplex_56_d),
    .bo(controled_subtract_mulyiplex_56_bo));
  controled_subtract_mulyiplex controled_subtract_mulyiplex_57 (
    .x(controled_subtract_mulyiplex_56_d), .y(in_2[1]), .os(OS3), .bi(controled_subtract_mulyiplex_60_bo),
    .d(controled_subtract_mulyiplex_57_d), .bo(controled_subtract_mulyiplex_57_bo));
  controled_subtract_mulyiplex controled_subtract_mulyiplex_58 (
    .x(controled_subtract_mulyiplex_62_d), .y(in_2[3]), .os(OS6), .bi(controled_subtract_mulyiplex_65_bo),
    .d(controled_subtract_mulyiplex_58_d), .bo(controled_subtract_mulyiplex_58_bo));
  controled_subtract_mulyiplex controled_subtract_mulyiplex_59 (
    .x(controled_subtract_mulyiplex_58_d), .y(in_2[4]), .os(OS7), .bi(controled_subtract_mulyiplex_66_bo),
    .d(R4), .bo(controled_subtract_mulyiplex_59_bo));
  controled_subtract_mulyiplex controled_subtract_mulyiplex_60 (
    .x(in_1[4]), .y(in_2[0]), .os(OS3), .bi(1'b0), .d(controled_subtract_mulyiplex_60_d),
    .bo(controled_subtract_mulyiplex_60_bo));
  controled_subtract_mulyiplex controled_subtract_mulyiplex_61 (
    .x(controled_subtract_mulyiplex_60_d), .y(in_2[1]), .os(OS4), .bi(controled_subtract_mulyiplex_63_bo),
    .d(controled_subtract_mulyiplex_61_d), .bo(controled_subtract_mulyiplex_61_bo));
  controled_subtract_mulyiplex controled_subtract_mulyiplex_62 (
    .x(controled_subtract_mulyiplex_61_d), .y(in_2[2]), .os(OS5), .bi(controled_subtract_mulyiplex_64_bo),
    .d(controled_subtract_mulyiplex_62_d), .bo(controled_subtract_mulyiplex_62_bo));
  controled_subtract_mulyiplex controled_subtract_mulyiplex_63 (
    .x(in_1[3]), .y(in_2[0]), .os(OS4), .bi(1'b0), .d(controled_subtract_mulyiplex_63_d),
    .bo(controled_subtract_mulyiplex_63_bo));
  controled_subtract_mulyiplex controled_subtract_mulyiplex_64 (
    .x(controled_subtract_mulyiplex_63_d), .y(in_2[1]), .os(OS5), .bi(controled_subtract_mulyiplex_67_bo),
    .d(controled_subtract_mulyiplex_64_d), .bo(controled_subtract_mulyiplex_64_bo));
  controled_subtract_mulyiplex controled_subtract_mulyiplex_65 (
    .x(controled_subtract_mulyiplex_64_d), .y(in_2[2]), .os(OS6), .bi(controled_subtract_mulyiplex_68_bo),
    .d(controled_subtract_mulyiplex_65_d), .bo(controled_subtract_mulyiplex_65_bo));
  controled_subtract_mulyiplex controled_subtract_mulyiplex_66 (
    .x(controled_subtract_mulyiplex_65_d), .y(in_2[3]), .os(OS7), .bi(controled_subtract_mulyiplex_69_bo),
    .d(R3), .bo(controled_subtract_mulyiplex_66_bo));
  controled_subtract_mulyiplex controled_subtract_mulyiplex_67 (
    .x(in_1[2]), .y(in_2[0]), .os(OS5), .bi(1'b0), .d(controled_subtract_mulyiplex_67_d),
    .bo(controled_subtract_mulyiplex_67_bo));
  controled_subtract_mulyiplex controled_subtract_mulyiplex_68 (
    .x(controled_subtract_mulyiplex_67_d), .y(in_2[1]), .os(OS6), .bi(controled_subtract_mulyiplex_70_bo),
    .d(controled_subtract_mulyiplex_68_d), .bo(controled_subtract_mulyiplex_68_bo));
  controled_subtract_mulyiplex controled_subtract_mulyiplex_69 (
    .x(controled_subtract_mulyiplex_68_d), .y(in_2[2]), .os(OS7), .bi(controled_subtract_mulyiplex_71_bo),
    .d(R2), .bo(controled_subtract_mulyiplex_69_bo));
  controled_subtract_mulyiplex controled_subtract_mulyiplex_70 (
    .x(in_1[1]), .y(in_2[0]), .os(OS6), .bi(1'b0), .d(controled_subtract_mulyiplex_70_d),
    .bo(controled_subtract_mulyiplex_70_bo));
  controled_subtract_mulyiplex controled_subtract_mulyiplex_71 (
    .x(controled_subtract_mulyiplex_70_d), .y(in_2[1]), .os(OS7), .bi(controled_subtract_mulyiplex_72_bo),
    .d(R1), .bo(controled_subtract_mulyiplex_71_bo));
  controled_subtract_mulyiplex controled_subtract_mulyiplex_72 (
    .x(in_1[0]), .y(in_2[0]), .os(OS7), .bi(1'b0), .d(R0), .bo(controled_subtract_mulyiplex_72_bo));

  // Other names for the same wires on the sheet: A0 = in_1[0]; A1 = in_1[1]; A2 = in_1[2]; A3 = in_1[3]; A4 = in_1[4];
  //   A5 = in_1[5]; A6 = in_1[6]; A7 = in_1[7]; B0 = in_2[0]; B1 = in_2[1]; B2 = in_2[2]; B3 = in_2[3]; B4 = in_2[4];
  //   B5 = in_2[5]; B6 = in_2[6]; B7 = in_2[7]
endmodule

module controled_subtract_mulyiplex (
  input  x,
  input  y,
  input  os,
  input  bi,
  output d,
  output bo
);

  wire and_1_out, and_2_out, and_3_out, and_4_out, d_star_out, not_1_out, not_2_out, not_3_out, xor_1_out;

  xor xor_1 (xor_1_out, x, y);
  not not_1 (not_1_out, x);
  and and_1 (and_1_out, not_1_out, y);
  not not_2 (not_2_out, xor_1_out);
  xor d_star (d_star_out, xor_1_out, bi);
  and and_2 (and_2_out, not_2_out, bi);
  or or_1 (bo, and_1_out, and_2_out);
  not not_3 (not_3_out, os);
  and and_3 (and_3_out, d_star_out, not_3_out);
  and and_4 (and_4_out, os, x);
  or or_2 (d, and_3_out, and_4_out);
endmodule

module hex_display (
  input  in_1,
  input  in_2,
  input  in_3,
  input  in_4,
  output out_5,
  output out_6,
  output out_7,
  output out_8,
  output out_9,
  output out_10,
  output out_11
);

  wire decoder_1_out0, decoder_1_out1, decoder_1_out2, decoder_1_out3, decoder_1_out4, decoder_1_out5,
       decoder_1_out6, decoder_1_out7, decoder_1_out8, decoder_1_out9, decoder_1_out10, decoder_1_out11,
       decoder_1_out12, decoder_1_out13, decoder_1_out14, decoder_1_out15;

  Decoder #(.select(4)) decoder_1 (
    .out0(decoder_1_out0), .out1(decoder_1_out1), .out2(decoder_1_out2), .out3(decoder_1_out3),
    .out4(decoder_1_out4), .out5(decoder_1_out5), .out6(decoder_1_out6), .out7(decoder_1_out7),
    .out8(decoder_1_out8), .out9(decoder_1_out9), .out10(decoder_1_out10), .out11(decoder_1_out11),
    .out12(decoder_1_out12), .out13(decoder_1_out13), .out14(decoder_1_out14), .out15(decoder_1_out15),
    .sel({in_4, in_3, in_2, in_1}), .en(1'b1));
  or A (out_5, decoder_1_out0, decoder_1_out1, decoder_1_out2, decoder_1_out3, decoder_1_out4, decoder_1_out7, decoder_1_out8, decoder_1_out9, decoder_1_out10, decoder_1_out13);
  or B (out_6, decoder_1_out0, decoder_1_out1, decoder_1_out3, decoder_1_out4, decoder_1_out5, decoder_1_out6, decoder_1_out7, decoder_1_out8, decoder_1_out9, decoder_1_out10, decoder_1_out11, decoder_1_out13);
  or C (out_7, decoder_1_out0, decoder_1_out2, decoder_1_out3, decoder_1_out5, decoder_1_out6, decoder_1_out8, decoder_1_out9, decoder_1_out11, decoder_1_out12, decoder_1_out13, decoder_1_out14);
  or D (out_8, decoder_1_out0, decoder_1_out2, decoder_1_out6, decoder_1_out8, decoder_1_out10, decoder_1_out11, decoder_1_out12, decoder_1_out13, decoder_1_out14, decoder_1_out15);
  or E (out_9, decoder_1_out0, decoder_1_out4, decoder_1_out5, decoder_1_out6, decoder_1_out8, decoder_1_out9, decoder_1_out10, decoder_1_out11, decoder_1_out12, decoder_1_out13, decoder_1_out14, decoder_1_out15);
  or F (out_10, decoder_1_out0, decoder_1_out2, decoder_1_out3, decoder_1_out5, decoder_1_out6, decoder_1_out7, decoder_1_out8, decoder_1_out9, decoder_1_out10, decoder_1_out12, decoder_1_out13, decoder_1_out14, decoder_1_out15);
  or G (out_11, decoder_1_out2, decoder_1_out3, decoder_1_out4, decoder_1_out5, decoder_1_out6, decoder_1_out8, decoder_1_out9, decoder_1_out10, decoder_1_out11, decoder_1_out14, decoder_1_out15);
endmodule
